// Logisim project VGA-OUT.circ as structural Verilog: 1 circuit, main circuit main
module main (
  input  CLOCK,
  input  [2:0] BG_COLOR,
  input  [7:0] DATAIN,
  output [1:0] BLUE,
  output HS,
  output [1:0] RED,
  output [1:0] GREEN,
  output VS,
  output [15:0] ADRESSS
);

  wire and_3_out, and_4_out, comparator_1_gt, comparator_2_lt, comparator_3_gt, comparator_4_lt,
       comparator_5_gt, comparator_6_lt, comparator_7_gt, comparator_8_lt, comparator_16_eq, flash,
       multiplexer_9_out, or_1_out, visible, vspaper, xmax, xon_e, xon_f, ymax;
  wire [2:0] BITN;
  wire [3:0] BG4, multiplexer_11_out, paper;
  wire [3:3] multiplexer_10_out;
  wire [5:0] adder_3_out, fcnt_q, multiplexer_5_out, multiplexer_6_out;
  wire [7:0] ATTR_q, CBUF_q, MASK_q, multiplexer_4_out, multiplexer_7_out, multiplexer_8_out;
  wire [9:0] adder_1_out, adder_2_out, ADDRESS_ATTR, multiplexer_1_out, multiplexer_2_out, multiplexer_3_out,
       X, x_t, Y, y_t;
  wire [10:8] ADDRESS_CHAR;

  Adder #(.width(10)) adder_1 (.a(Y), .b(10'h1), .out(adder_1_out));  // open: cin, cout
  Adder #(.width(10)) adder_2 (.a(X), .b(10'h1), .out(adder_2_out));  // open: cin, cout
  Multiplexer #(.width(10)) multiplexer_1 (
    .in0(adder_2_out), .in1({10{1'b0}}), .out(multiplexer_1_out), .sel(xmax));  // open: en
  Multiplexer #(.width(10)) multiplexer_2 (
    .in0(adder_1_out), .in1({10{1'b0}}), .out(multiplexer_2_out), .sel(ymax));  // open: en
  Comparator #(.width(10), .mode("unsigned")) comparator_1 (.a(X), .b(10'h2f), .gt(comparator_1_gt));  // open: eq, lt
  Comparator #(.width(10), .mode("unsigned")) comparator_2 (.a(X), .b(10'h2b0), .lt(comparator_2_lt));  // open: gt, eq
  Comparator #(.width(10), .mode("unsigned")) comparator_3 (.a(Y), .b(10'h20), .gt(comparator_3_gt));  // open: eq, lt
  Comparator #(.width(10), .mode("unsigned")) comparator_4 (.a(Y), .b(10'h201), .lt(comparator_4_lt));  // open: gt, eq
  Comparator #(.width(10), .mode("unsigned")) comparator_5 (.a(X), .b(10'h6f), .gt(comparator_5_gt));  // open: eq, lt
  Comparator #(.width(10), .mode("unsigned")) comparator_6 (.a(X), .b(10'h270), .lt(comparator_6_lt));  // open: gt, eq
  Comparator #(.width(10), .mode("unsigned")) comparator_7 (.a(Y), .b(10'h4f), .gt(comparator_7_gt));  // open: eq, lt
  Comparator #(.width(10), .mode("unsigned")) comparator_8 (.a(Y), .b(10'h1d0), .lt(comparator_8_lt));  // open: gt, eq
  assign BG4 = {{1{1'b0}}, BG_COLOR};  // Bit_Extender bit_extender_1
  Register #(.width(10)) u_X (.D(multiplexer_1_out), .Q(X), .clk(CLOCK));  // open: en, clr
  Register #(.width(10)) u_Y (.D(multiplexer_3_out), .Q(Y), .clk(CLOCK));  // open: en, clr
  Multiplexer #(.width(10)) multiplexer_3 (
    .in0(Y), .in1(multiplexer_2_out), .out(multiplexer_3_out), .sel(xmax));  // open: en
  and and_1 (visible, comparator_1_gt, comparator_2_lt, comparator_3_gt, comparator_4_lt);
  Comparator #(.width(10), .mode("unsigned")) comparator_9 (.a(X), .b(10'h2c0), .lt(HS));  // open: gt, eq
  Comparator #(.width(10), .mode("unsigned")) comparator_10 (.a(X), .b(10'h31f), .eq(xmax));  // open: gt, lt
  Comparator #(.width(10), .mode("unsigned")) comparator_11 (.a(Y), .b(10'h20a), .gt(VS));  // open: eq, lt
  Comparator #(.width(10), .mode("unsigned")) comparator_12 (.a(Y), .b(10'h20c), .eq(ymax));  // open: gt, lt
  and and_2 (vspaper, comparator_5_gt, comparator_6_lt, comparator_7_gt, comparator_8_lt);
  Multiplexer #(.width(8)) multiplexer_4 (
    .in0(CBUF_q), .in1(DATAIN), .out(multiplexer_4_out), .sel(xon_e));  // open: en
  Adder #(.width(6)) adder_3 (.a(fcnt_q), .b(6'b000001), .out(adder_3_out));  // open: cin, cout
  Multiplexer #(.width(6)) multiplexer_5 (
    .in0(adder_3_out), .in1({6{1'b0}}), .out(multiplexer_5_out), .sel(comparator_16_eq));  // open: en
  Comparator #(.width(4)) comparator_13 (.a({BITN, x_t[0]}), .b(4'b1110), .eq(xon_e));  // open: gt, lt
  Comparator #(.width(4)) comparator_14 (.a({BITN, x_t[0]}), .b(4'b1111), .eq(xon_f));  // open: gt, lt
  Register CBUF (.D(multiplexer_4_out), .Q(CBUF_q), .clk(CLOCK));  // open: en, clr
  Multiplexer #(.width(6)) multiplexer_6 (
    .in0(fcnt_q), .in1(multiplexer_5_out), .out(multiplexer_6_out), .sel(and_3_out));  // open: en
  Register #(.width(6)) fcnt (.D(multiplexer_6_out), .Q(fcnt_q), .clk(CLOCK));  // open: en, clr
  and and_3 (and_3_out, xmax, ymax);
  Register MASK (.D(multiplexer_7_out), .Q(MASK_q), .clk(CLOCK));  // open: en, clr
  Multiplexer #(.width(8)) multiplexer_7 (
    .in0(MASK_q), .in1(CBUF_q), .out(multiplexer_7_out), .sel(xon_f));  // open: en
  Register ATTR (.D(multiplexer_8_out), .Q({ATTR_q[7], paper[3], ATTR_q[5:0]}), .clk(CLOCK));  // open: en, clr
  Multiplexer #(.width(8)) multiplexer_8 (
    .in0({ATTR_q[7], paper[3], ATTR_q[5:0]}), .in1(DATAIN), .out(multiplexer_8_out), .sel(xon_f));  // open: en
  Comparator #(.width(6), .mode("unsigned")) comparator_15 (.a(fcnt_q), .b(6'b011000), .gt(flash));  // open: eq, lt
  Comparator #(.width(6), .mode("unsigned")) comparator_16 (
    .a(fcnt_q), .b(6'b110001), .eq(comparator_16_eq));  // open: gt, lt
  Subtractor #(.width(10)) subtractor_1 (
    .a(X), .b(10'h60), .out({x_t[9], ADDRESS_ATTR[4:0], BITN, x_t[0]}));  // open: bin, bout
  Subtractor #(.width(10)) subtractor_2 (
    .a(Y), .b(10'h50), .out({y_t[9], ADDRESS_ATTR[9:5], ADDRESS_CHAR, y_t[0]}));  // open: bin, bout
  Multiplexer #(.select(3)) multiplexer_9 (
    .in0(MASK_q[0]), .in1(MASK_q[1]), .in2(MASK_q[2]), .in3(MASK_q[3]), .in4(MASK_q[4]), .in5(MASK_q[5]),
    .in6(MASK_q[6]), .in7(MASK_q[7]), .out(multiplexer_9_out), .sel(BITN));  // open: en
  and and_4 (and_4_out, ATTR_q[7], flash);
  or or_1 (or_1_out, multiplexer_9_out, and_4_out);
  Multiplexer #(.width(4)) multiplexer_10 (
    .in0(4'b0000), .in1(multiplexer_11_out), .out({multiplexer_10_out[3], GREEN[0], RED[0], BLUE[0]}),
    .sel(visible));  // open: en
  Multiplexer #(.width(4)) multiplexer_11 (
    .in0(BG4), .in1(paper), .out(multiplexer_11_out), .sel(vspaper));  // open: en
  Multiplexer #(.width(3)) multiplexer_12 (
    .in0(ATTR_q[5:3]), .in1(ATTR_q[2:0]), .out(paper[2:0]), .sel(or_1_out));  // open: en
  Multiplexer #(.width(16)) multiplexer_13 (
    .in0({3'b010, ADDRESS_ATTR[9:8], ADDRESS_CHAR, ADDRESS_ATTR[7:0]}), .in1({6'b010110, ADDRESS_ATTR}),
    .out(ADRESSS), .sel(xon_e));  // open: en
  and and_5 (BLUE[1], BLUE[0], multiplexer_10_out[3]);
  and and_6 (RED[1], RED[0], multiplexer_10_out[3]);
  and and_7 (GREEN[1], GREEN[0], multiplexer_10_out[3]);

  // Other names for the same wires on the sheet: ADDRESS_CHAR (some bits) = ADDRESS_ATTR;
  //   x_t[8:1] = {ADDRESS_ATTR[4:0], BITN}; y_t[8:1] = {ADDRESS_ATTR[9:5], ADDRESS_CHAR}; CLK = CLOCK

  // Notes on the sheet:
  //   Опорный видеосигнал
  //   Данные из памяти
  //   Область PAPER
  //   xmax
  //   ymax
  //   Видимая область
  //   Буфер Mask
  //   Генерация мерцаний символов
  //   Выбор режима записи
  //   fmax
  //   Генератор видеоадреса
  //   invert
  //   Генератор конечного цвета
  //   Генератор цвета на области PAPER
  //   bright
endmodule
